# Fritzing sketch 1 (saved by Fritzing 0.9.3b)
breadboards: 1

parts:
  LM741 = LM386 [package=dip08]
  R3 = Rotary Potentiometer (Small) [maximum_resistance=100k package=THT]
  T2 = Resistor [tolerance=±5% resistance=100k package=THT]
  T1 = Resistor [tolerance=±5% resistance=100k package=THT]
  J1 = female pin header, 2 pins [form="♀ (female)"]
  R4 = Resistor [tolerance=±5% resistance=1k package=THT]
  R5 = Resistor [tolerance=±5% resistance=4.7k package=THT]

nets:
  N1: LM741.-IN, R4.Pin_1, R5.Pin_0
  N2: LM741.+IN, T2.Pin_0, T1.Pin_1
  GND: LM741.V-, R3.leg1, T1.Pin_0, J1.pin2
  N3: LM741.OUT, J1.pin1, R5.Pin_1
  12V: LM741.V+, R3.leg2, T2.Pin_1
  N4: R3.wiper, R4.Pin_0
