# Fritzing sketch 2 (saved by Fritzing 0.9.3b)
breadboards: 1

parts:
  Continuity_Sensor = female pin header, 2 pins [form="♀ (female)"]
  D400 = TRANSISTOR_NPN [package=to-92]
  Heater = Inductor [package="400 mil [THT]"]
  R1 = Resistor [tolerance=±5% resistance=1k package=THT]
  R2 = Resistor [tolerance=±5% resistance=10k package=THT]

nets:
  12V: Continuity_Sensor.pin1, Heater.pin_0
  N1: Continuity_Sensor.pin2, R1.Pin_0, R2.Pin_1
  GND: D400.E, R2.Pin_0
  N2: D400.B, R1.Pin_1
  N3: D400.C, Heater.pin_1
